// Logisim project circuit.circ as structural Verilog: 1 circuit, main circuit main
module main (
);

  wire button_1_out, clock_1_out;
  wire [7:0] adder_1_out, adder_2_out, bit_extender_1_out, bit_extender_2_out, multiplexer_1_out,
       multiplexer_2_out, multiplexer_3_out, multiplexer_4_out, register_1_q, register_2_q, rom_1_data,
       subtractor_1_out, subtractor_2_out;

  Clock clock_1 (.out(clock_1_out));
  Register register_1 (.D(adder_1_out), .en(1'b1), .clk(clock_1_out), .Q(register_1_q), .clr(button_1_out));
  Button button_1 (.out(button_1_out));
  ROM rom_1 (.addr(register_1_q), .data(rom_1_data));
  Adder adder_1 (.a(register_1_q), .b({8{1'b0}}), .out(adder_1_out), .cin(1'b1));  // open: cout
  Register register_2 (.D(multiplexer_4_out), .en(1'b1), .clk(clock_1_out), .Q(register_2_q), .clr(button_1_out));
  assign bit_extender_1_out = {{3{1'b0}}, rom_1_data[4:0]};  // Bit_Extender bit_extender_1
  assign bit_extender_2_out = {{1{rom_1_data[6]}}, rom_1_data[6:0]};  // Bit_Extender bit_extender_2
  Adder adder_2 (.a(register_2_q), .b(bit_extender_1_out), .out(adder_2_out));  // open: cin, cout
  Subtractor subtractor_1 (.a(register_2_q), .b(bit_extender_1_out), .out(subtractor_1_out));  // open: bin, bout
  Multiplexer #(.width(8)) multiplexer_1 (
    .in0(register_2_q), .in1(subtractor_2_out), .out(multiplexer_1_out), .sel(register_2_q[7]));
  Subtractor subtractor_2 (.a({8{1'b0}}), .b(register_2_q), .out(subtractor_2_out));  // open: bin, bout
  Multiplexer #(.width(8)) multiplexer_2 (
    .in0(register_2_q), .in1({8{1'b0}}), .out(multiplexer_2_out), .sel(register_2_q[7]));
  Multiplexer #(.select(2), .width(8)) multiplexer_3 (
    .in0(adder_2_out), .in1(subtractor_1_out), .in2(multiplexer_1_out), .in3(multiplexer_2_out),
    .out(multiplexer_3_out), .sel(rom_1_data[6:5]));
  Multiplexer #(.width(8)) multiplexer_4 (
    .in0(multiplexer_3_out), .in1(bit_extender_2_out), .out(multiplexer_4_out), .sel(rom_1_data[7]));

  // Notes on the sheet:
  //   contents of rom_1 (hex, n*v repeats v):
  //   83 2 28 40 2b 60 1 ff
  //   MUX3
  //   MUX4
  //   MUX1
  //   MUX2
endmodule
